# Fritzing sketch fine-dust (saved by Fritzing 0.9.3b)
breadboards: 1

parts:
  부품1 = Arduino Uno (Rev3)
  LCD1 = LCD screen
  R1 = Rotary Potentiometer (Small) [maximum_resistance=10kΩ package=THT]
  R2 = Resistor [tolerance=±5% resistance=220 package="0603 [SMD]"]
  BT1 = Bluetooth HC-06u [package=THT]

nets:
  N1: 부품1.D8, LCD1.DB2
  N2: 부품1.D9_PWM, LCD1.DB3
  N3: 부품1.D10_PWM/SS, LCD1.DB4
  N4: 부품1.D11_PWM/MOSI, LCD1.DB5
  N5: 부품1.D12/MISO, LCD1.DB6
  N6: 부품1.D13/SCK, LCD1.DB7
  N7: 부품1.D0/RX, BT1.TXD
  N8: 부품1.D1/TX, BT1.RXD
  N9: 부품1.D3_PWM, LCD1.RS
  N10: 부품1.D4, LCD1.R/W
  N11: 부품1.D5_PWM, LCD1.E
  N12: 부품1.D6_PWM, LCD1.DB0
  N13: 부품1.D7, LCD1.DB1
  5V: 부품1.5V, LCD1.VDD, R1.leg1, R2.Pin_1, BT1.VCC
  GND: 부품1.GND, LCD1.VSS, LCD1.LED-, R1.leg2, BT1.GND
  N14: LCD1.V0, R1.wiper
  N15: LCD1.LED+, R2.Pin_0

notes:
  PM2008M Sensor

custom parts:
  Bluetooth HC-06u: Bluetooth HC-06 - face up, pins down 16.5mm x 37.5mm PCB
